# Fritzing sketch TempWarningCircuit (saved by Fritzing 0.8.3b)
breadboards: 1

parts:
  Part1 = Arduino Uno (Rev3)
  T1 = LM35 Temperature Sensor [package="TO92 [THT]"]
  R1 = Resistor [tolerance=±5% resistance=220 package=THT]
  LED1 = LED - 5mm [color="Red (633nm)" package="5 mm [THT]"]

nets:
  N1: Part1.A0, T1.Vout
  N2: Part1.ICSP_SCK, Part1.D13/SCK, LED1.anode
  GND: Part1.GND, T1.GND, R1.Pin_1
  N3: Part1.5V, T1.+Vs
  N4: R1.Pin_0, LED1.cathode
